// Logisim project JCore1.circ as structural Verilog: 13 circuits, main circuit JC11BAOXN
module JC11BAOXN (
  input  [1:0] OP,
  input  A,
  input  B,
  output O
);

  wire and_1_out, nor_1_out, or_1_out, xor_1_out;

  and and_1 (and_1_out, A, B);
  or or_1 (or_1_out, A, B);
  xor xor_1 (xor_1_out, A, B);
  nor nor_1 (nor_1_out, A, B);
  Multiplexer #(.select(2)) multiplexer_1 (
    .in0(and_1_out), .in1(or_1_out), .in2(xor_1_out), .in3(nor_1_out), .out(O), .sel(OP));
endmodule

module JC18BAOXN (
  input  [7:0] B,
  input  [1:0] Op,
  input  [7:0] A,
  output [7:0] out_4
);

  JC11BAOXN jc11baoxn_1 (.A(A[0]), .B(B[0]), .OP(Op), .O(out_4[0]));
  JC11BAOXN jc11baoxn_2 (.A(A[1]), .B(B[1]), .OP(Op), .O(out_4[1]));
  JC11BAOXN jc11baoxn_3 (.A(A[2]), .B(B[2]), .OP(Op), .O(out_4[2]));
  JC11BAOXN jc11baoxn_4 (.A(A[3]), .B(B[3]), .OP(Op), .O(out_4[3]));
  JC11BAOXN jc11baoxn_5 (.A(A[4]), .B(B[4]), .OP(Op), .O(out_4[4]));
  JC11BAOXN jc11baoxn_6 (.A(A[5]), .B(B[5]), .OP(Op), .O(out_4[5]));
  JC11BAOXN jc11baoxn_7 (.A(A[6]), .B(B[6]), .OP(Op), .O(out_4[6]));
  JC11BAOXN jc11baoxn_8 (.A(A[7]), .B(B[7]), .OP(Op), .O(out_4[7]));
endmodule

module test (
  input  [1:0] in_1,
  input  [63:0] in_2,
  input  [63:0] in_3,
  input  [63:0] in_4,
  input  in_5,
  output [63:0] out_6,
  output [63:0] out_7,
  output [63:0] out_8,
  output [63:0] out_9
);

  wire clock_1_out;
  wire [63:0] random_1_out;

  Clock clock_1 (.out(clock_1_out));
  Random #(.width(64)) random_1 (.clr(1'b0), .next(1'b1), .clk(clock_1_out), .out(random_1_out));
  JC14REG256 jc14reg256_1 (
    .DI0(random_1_out), .DI1(in_2), .DI2(in_3), .DI3(in_4), .REGID(in_1), .WE(in_5), .DO0(out_6),
    .DO1(out_7), .DO2(out_8), .DO3(out_9));
endmodule

module JC1FFBAOXN (
  input  [63:0] B,
  input  [1:0] Op,
  input  [63:0] A,
  output [63:0] out_4
);

  JC18BAOXN jc18baoxn_1 (.A(A[7:0]), .B(B[7:0]), .Op(Op), .out_4(out_4[7:0]));
  JC18BAOXN jc18baoxn_2 (.A(A[15:8]), .B(B[15:8]), .Op(Op), .out_4(out_4[15:8]));
  JC18BAOXN jc18baoxn_3 (.A(A[23:16]), .B(B[23:16]), .Op(Op), .out_4(out_4[23:16]));
  JC18BAOXN jc18baoxn_4 (.A(A[31:24]), .B(B[31:24]), .Op(Op), .out_4(out_4[31:24]));
  JC18BAOXN jc18baoxn_5 (.A(A[39:32]), .B(B[39:32]), .Op(Op), .out_4(out_4[39:32]));
  JC18BAOXN jc18baoxn_6 (.A(A[47:40]), .B(B[47:40]), .Op(Op), .out_4(out_4[47:40]));
  JC18BAOXN jc18baoxn_7 (.A(A[55:48]), .B(B[55:48]), .Op(Op), .out_4(out_4[55:48]));
  JC18BAOXN jc18baoxn_8 (.A(A[63:56]), .B(B[63:56]), .Op(Op), .out_4(out_4[63:56]));
endmodule

module JC11BOTP (
  input  DIN,
  input  CLK,
  output DOUT,
  output KOUT
);

  Random #(.seed(2), .width(1)) random_1 (.clr(1'b0), .next(1'b1), .clk(CLK), .out(KOUT));
  JC11BAOXN jc11baoxn_1 (.A(DIN), .B(KOUT), .OP(2'b11), .O(DOUT));
endmodule

module JC11BADD (
  input  A,
  input  B,
  input  Cin,
  output S,
  output Cout
);

  wire and_1_out, and_2_out, xor_1_out;

  xor xor_1 (xor_1_out, A, B);
  and and_1 (and_1_out, Cin, xor_1_out);
  and and_2 (and_2_out, B, A);
  xor xor_2 (S, xor_1_out, Cin);
  or or_1 (Cout, and_1_out, and_2_out);
endmodule

module JC18BADD (
  input  [7:0] A,
  input  [7:0] B,
  input  Cin,
  output [7:0] S,
  output Cout
);

  wire jc11badd_1_cout, jc11badd_2_cout, jc11badd_3_cout, jc11badd_4_cout, jc11badd_5_cout, jc11badd_6_cout,
       jc11badd_7_cout;

  JC11BADD jc11badd_1 (.A(A[0]), .B(B[0]), .Cin(Cin), .S(S[0]), .Cout(jc11badd_1_cout));
  JC11BADD jc11badd_2 (.A(A[1]), .B(B[1]), .Cin(jc11badd_1_cout), .S(S[1]), .Cout(jc11badd_2_cout));
  JC11BADD jc11badd_3 (.A(A[2]), .B(B[2]), .Cin(jc11badd_2_cout), .S(S[2]), .Cout(jc11badd_3_cout));
  JC11BADD jc11badd_4 (.A(A[3]), .B(B[3]), .Cin(jc11badd_3_cout), .S(S[3]), .Cout(jc11badd_4_cout));
  JC11BADD jc11badd_5 (.A(A[4]), .B(B[4]), .Cin(jc11badd_4_cout), .S(S[4]), .Cout(jc11badd_5_cout));
  JC11BADD jc11badd_6 (.A(A[5]), .B(B[5]), .Cin(jc11badd_5_cout), .S(S[5]), .Cout(jc11badd_6_cout));
  JC11BADD jc11badd_7 (.A(A[6]), .B(B[6]), .Cin(jc11badd_6_cout), .S(S[6]), .Cout(jc11badd_7_cout));
  JC11BADD jc11badd_8 (.A(A[7]), .B(B[7]), .Cin(jc11badd_7_cout), .S(S[7]), .Cout(Cout));
endmodule

module JC1FFBADD (
  input  [63:0] A,
  input  [63:0] B,
  input  Cin,
  output [63:0] S,
  output Cout
);

  wire jc18badd_1_cout, jc18badd_2_cout, jc18badd_3_cout, jc18badd_4_cout, jc18badd_5_cout, jc18badd_6_cout,
       jc18badd_7_cout;

  JC18BADD jc18badd_1 (.B(B[7:0]), .Cin(Cin), .A(A[7:0]), .Cout(jc18badd_1_cout), .S(S[7:0]));
  JC18BADD jc18badd_2 (.B(B[15:8]), .Cin(jc18badd_1_cout), .A(A[15:8]), .Cout(jc18badd_2_cout), .S(S[15:8]));
  JC18BADD jc18badd_3 (.B(B[23:16]), .Cin(jc18badd_2_cout), .A(A[23:16]), .Cout(jc18badd_3_cout), .S(S[23:16]));
  JC18BADD jc18badd_4 (.B(B[31:24]), .Cin(jc18badd_3_cout), .A(A[31:24]), .Cout(jc18badd_4_cout), .S(S[31:24]));
  JC18BADD jc18badd_5 (.B(B[39:32]), .Cin(jc18badd_4_cout), .A(A[39:32]), .Cout(jc18badd_5_cout), .S(S[39:32]));
  JC18BADD jc18badd_6 (.B(B[47:40]), .Cin(jc18badd_5_cout), .A(A[47:40]), .Cout(jc18badd_6_cout), .S(S[47:40]));
  JC18BADD jc18badd_7 (.B(B[55:48]), .Cin(jc18badd_6_cout), .A(A[55:48]), .Cout(jc18badd_7_cout), .S(S[55:48]));
  JC18BADD jc18badd_8 (.B(B[63:56]), .Cin(jc18badd_7_cout), .A(A[63:56]), .Cout(Cout), .S(S[63:56]));
endmodule

module JC1LATCH1 (
  input  DI,
  input  WE,
  output DO
);

  wire and_1_out, and_2_out, nor_1_out, not_1_out;

  not not_1 (not_1_out, DI);
  and and_1 (and_1_out, DI, WE);
  and and_2 (and_2_out, not_1_out, WE);
  nor nor_1 (nor_1_out, and_1_out, DO);
  nor nor_2 (DO, nor_1_out, and_2_out);
endmodule

module JC1REG18 (
  input  [7:0] DI,
  input  WE,
  output [7:0] out_3
);

  JC1LATCH1 jc1latch1_1 (.WE(WE), .DI(DI[0]), .DO(out_3[0]));
  JC1LATCH1 jc1latch1_2 (.WE(WE), .DI(DI[1]), .DO(out_3[1]));
  JC1LATCH1 jc1latch1_3 (.WE(WE), .DI(DI[2]), .DO(out_3[2]));
  JC1LATCH1 jc1latch1_4 (.WE(WE), .DI(DI[3]), .DO(out_3[3]));
  JC1LATCH1 jc1latch1_5 (.WE(WE), .DI(DI[4]), .DO(out_3[4]));
  JC1LATCH1 jc1latch1_6 (.WE(WE), .DI(DI[5]), .DO(out_3[5]));
  JC1LATCH1 jc1latch1_7 (.WE(WE), .DI(DI[6]), .DO(out_3[6]));
  JC1LATCH1 jc1latch1_8 (.WE(WE), .DI(DI[7]), .DO(out_3[7]));
endmodule

module JC1REG164 (
  input  [63:0] DI,
  input  WE,
  output [63:0] DO
);

  JC1REG18 jc1reg18_1 (.WE(WE), .DI(DI[7:0]), .out_3(DO[7:0]));
  JC1REG18 jc1reg18_2 (.WE(WE), .DI(DI[15:8]), .out_3(DO[15:8]));
  JC1REG18 jc1reg18_3 (.WE(WE), .DI(DI[23:16]), .out_3(DO[23:16]));
  JC1REG18 jc1reg18_4 (.WE(WE), .DI(DI[31:24]), .out_3(DO[31:24]));
  JC1REG18 jc1reg18_5 (.WE(WE), .DI(DI[39:32]), .out_3(DO[39:32]));
  JC1REG18 jc1reg18_6 (.WE(WE), .DI(DI[47:40]), .out_3(DO[47:40]));
  JC1REG18 jc1reg18_7 (.WE(WE), .DI(DI[55:48]), .out_3(DO[55:48]));
  JC1REG18 jc1reg18_8 (.WE(WE), .DI(DI[63:56]), .out_3(DO[63:56]));
endmodule

module JC1REG1256 (
  input  [63:0] DI0,
  input  [63:0] DI1,
  input  [63:0] DI2,
  input  [63:0] DI3,
  input  WE,
  output [63:0] DO0,
  output [63:0] DO1,
  output [63:0] DO2,
  output [63:0] DO3
);

  JC1REG164 jc1reg164_1 (.WE(WE), .DI(DI0), .DO(DO0));
  JC1REG164 jc1reg164_2 (.WE(WE), .DI(DI1), .DO(DO1));
  JC1REG164 jc1reg164_3 (.WE(WE), .DI(DI2), .DO(DO2));
  JC1REG164 jc1reg164_4 (.WE(WE), .DI(DI3), .DO(DO3));
endmodule

module JC14REG256 (
  input  [1:0] REGID,
  input  WE,
  input  [63:0] DI0,
  input  [63:0] DI1,
  input  [63:0] DI2,
  input  [63:0] DI3,
  output [63:0] DO0,
  output [63:0] DO1,
  output [63:0] DO2,
  output [63:0] DO3
);

  wire and_1_out, and_2_out, and_3_out, and_4_out, decoder_1_out0, decoder_1_out1, decoder_1_out2,
       decoder_1_out3;
  wire [63:0] jc1reg1256_1_do0, jc1reg1256_1_do1, jc1reg1256_1_do2, jc1reg1256_1_do3, jc1reg1256_2_do0,
       jc1reg1256_2_do1, jc1reg1256_2_do2, jc1reg1256_2_do3, jc1reg1256_3_do0, jc1reg1256_3_do1,
       jc1reg1256_3_do2, jc1reg1256_3_do3, jc1reg1256_4_do0, jc1reg1256_4_do1, jc1reg1256_4_do2,
       jc1reg1256_4_do3;

  and and_1 (and_1_out, decoder_1_out0, WE);
  Multiplexer #(.select(2), .width(64)) multiplexer_1 (
    .in0(jc1reg1256_1_do0), .in1(jc1reg1256_2_do0), .in2(jc1reg1256_3_do0), .in3(jc1reg1256_4_do0),
    .out(DO0), .sel(REGID));
  Decoder #(.select(2)) decoder_1 (
    .out0(decoder_1_out0), .out1(decoder_1_out1), .out2(decoder_1_out2), .out3(decoder_1_out3), .sel(REGID));  // open: en
  and and_2 (and_2_out, decoder_1_out1, WE);
  JC1REG1256 jc1reg1256_1 (
    .WE(and_1_out), .DI1(DI1), .DI2(DI2), .DI3(DI3), .DI0(DI0), .DO1(jc1reg1256_1_do1),
    .DO2(jc1reg1256_1_do2), .DO3(jc1reg1256_1_do3), .DO0(jc1reg1256_1_do0));
  JC1REG1256 jc1reg1256_2 (
    .WE(and_2_out), .DI1(DI1), .DI2(DI2), .DI3(DI3), .DI0(DI0), .DO1(jc1reg1256_2_do1),
    .DO2(jc1reg1256_2_do2), .DO3(jc1reg1256_2_do3), .DO0(jc1reg1256_2_do0));
  Multiplexer #(.select(2), .width(64)) multiplexer_2 (
    .in0(jc1reg1256_1_do1), .in1(jc1reg1256_2_do1), .in2(jc1reg1256_3_do1), .in3(jc1reg1256_4_do1),
    .out(DO1), .sel(REGID));
  and and_3 (and_3_out, WE, decoder_1_out2);
  Multiplexer #(.select(2), .width(64)) multiplexer_3 (
    .in0(jc1reg1256_1_do2), .in1(jc1reg1256_2_do2), .in2(jc1reg1256_3_do2), .in3(jc1reg1256_4_do2),
    .out(DO2), .sel(REGID));
  and and_4 (and_4_out, WE, decoder_1_out3);
  Multiplexer #(.select(2), .width(64)) multiplexer_4 (
    .in0(jc1reg1256_1_do3), .in1(jc1reg1256_2_do3), .in2(jc1reg1256_3_do3), .in3(jc1reg1256_4_do3),
    .out(DO3), .sel(REGID));
  JC1REG1256 jc1reg1256_3 (
    .WE(and_3_out), .DI1(DI1), .DI2(DI2), .DI3(DI3), .DI0(DI0), .DO1(jc1reg1256_3_do1),
    .DO2(jc1reg1256_3_do2), .DO3(jc1reg1256_3_do3), .DO0(jc1reg1256_3_do0));
  JC1REG1256 jc1reg1256_4 (
    .WE(and_4_out), .DI1(DI1), .DI2(DI2), .DI3(DI3), .DI0(DI0), .DO1(jc1reg1256_4_do1),
    .DO2(jc1reg1256_4_do2), .DO3(jc1reg1256_4_do3), .DO0(jc1reg1256_4_do0));
endmodule
